# Fritzing sketch 555變壓器激磁 (saved by Fritzing 0.9.3b)
breadboards: 1

parts:
  IC1 = General purpose bipolar Timer [package=dil-08]
  R1 = Resistor [tolerance=±5% resistance=1k package="1206 [SMD]"]
  R2 = Resistor [tolerance=±5% resistance=22k package="1206 [SMD]"]
  C1 = Capacitor [package=cap-pth-small]
  R3 = Resistor [tolerance=±5% resistance=4.7k package="1206 [SMD]"]
  R4 = Resistor [tolerance=±5% resistance=10k package="1206 [SMD]"]
  C2 = Capacitor Polarized [package=cpol-radial-100uf-25v]

nets:
  N1: IC1.GND, C1.2, R4.Pin_1, C2.-
  N2: IC1.TRI, IC1.TRE, R2.Pin_1, C2.+
  N3: IC1.OUT, R3.Pin_0, R4.Pin_0
  N4: IC1._RES, IC1.VCC+, R1.Pin_0
  N5: IC1.CON, C1.1
  N6: IC1.DIS, R1.Pin_1, R2.Pin_0

notes:
  1KΩ
  22KΩ
  103 / 0.01㎌
  555
  12V
  GND
  10KΩ
  4.7KΩ
  接到7404腳1
  320hz / 51.11% duty
  0.1 / 50V ㎌
  By 羽山 https://3wa.tw
  555 激磁脈波產生器
