# Fritzing sketch NSR_CDI_TESTER電路圖V0.01 (saved by Fritzing 0.9.3b)
breadboards: 2

parts:
  U1 = attiny85 [package=dip]
  元件1 = TM1637
  R1 = Rotary Potentiometer (Large) [maximum_resistance=100kΩ package=THT]
  R2 = Resistor [tolerance=±5% resistance=100 package="0402 [SMD]"]
  LED1 = LED - 5mm [color="Red (633nm)" package="5 mm [THT]"]
  U2 = Sharp PC817 [package=THT]
  R3 = Resistor [tolerance=±5% resistance=10k package=THT]
  R4 = Resistor [tolerance=±5% resistance=10k package=THT]
  U3 = Transformer [package=transformer]
  U4 = Mini-360 DC-DC Buck converter [package=THT]
  R5 = Resistor [tolerance=±5% resistance=4.7k package=THT]  # not connected
  IC1 = 74LS04 [chip_label=IC package="DIP (Dual Inline) [THT]"]
  IC1_A = 74LS04 [package="DIP (Dual Inline) [THT]"]  # not connected
  IC1_B = 74LS04 [package="DIP (Dual Inline) [THT]"]  # not connected
  IC1_C = 74LS04 [package="DIP (Dual Inline) [THT]"]  # not connected
  IC1_D = 74LS04 [package="DIP (Dual Inline) [THT]"]  # not connected
  IC1_E = 74LS04 [package="DIP (Dual Inline) [THT]"]  # not connected
  IC1_F = 74LS04 [package="DIP (Dual Inline) [THT]"]  # not connected
  IC1_PWR = 74LS04 [package="DIP (Dual Inline) [THT]"]  # not connected
  R6 = Resistor [tolerance=±5% resistance=220 package=THT]  # not connected
  R7 = Resistor [tolerance=±5% resistance=220 package=THT]  # not connected
  Q1 = TRANSISTOR_NPN [package=to-92]
  R8 = Resistor [tolerance=±5% resistance=10k package=THT]
  R9 = Resistor [tolerance=±5% resistance=10k package=THT]
  Q2 = TRANSISTOR_NPN [package=to-92]
  R10 = Resistor [tolerance=±5% resistance=10k package=THT]
  Q3 = TRANSISTOR_NPN [package=to-92]
  Q4 = TRANSISTOR_NPN [package=to-92]
  R11 = Resistor [tolerance=±5% resistance=1k package=THT]
  R12 = Resistor [tolerance=±5% resistance=1k package=THT]
  U5 = Transformer [package=transformer]

nets:
  N1: U1.Pin_2, R1.wiper
  N2: U1.Pin_3, R2.Pin_0
  N3: U1.Pin_4, 元件1.VCC, R1.leg2, U2.Pin_2, R3.Pin_0, U4.OUT-
  N4: U1.Pin_5, 元件1.CLK
  N5: U1.Pin_6, 元件1.DIO
  N6: U1.Pin_8, 元件1.GND, R1.leg1, IC1.connector13
  N7: R2.Pin_1, LED1.anode
  N8: LED1.cathode, U2.Pin_1, R3.Pin_1
  N9: U2.Pin_3, R4.Pin_0
  N10: R4.Pin_1, U3.3, U5.4
  N11: U4.IN-, IC1.connector6, Q1.E, R8.Pin_1, Q2.E, Q3.C, Q4.C
  N12: IC1.connector0, R8.Pin_0
  N13: IC1.connector1, IC1.connector2
  N14: Q1.B, R9.Pin_0, R11.Pin_1
  N15: R9.Pin_1, R10.Pin_1
  N16: Q2.B, R10.Pin_0, R12.Pin_1
  N17: Q3.E, R11.Pin_0
  N18: Q4.E, R12.Pin_0

notes:
  接 CDI 4P 右上(青黃) 脈衝
  NSR-150
  CDI 點火測試機
  By 羽山 https://3wa.tw
  LED
  10KΩ
  PC817
  TM1637
  ATTiny 85
  VR 10KΩ
  100Ω
  小型變壓器
  ST-20 (600:1K)
  第二組獨立電源
  VCC 5V
  GND
  可用 USB 豆腐頭
  第一組獨立電源
  VCC 12V
  GND
  BUCK
  MP1584
  12V 轉 5V
  VCC 5V
  GND
  74LS04
  10KΩ
  4.7KΩ
  220Ω
  220Ω
  C945
  C945
  腳BCE
  IRLZ48N
  IRLZ48N
  腳GDS
  中心抽頭
  變壓器
  12-0-12
  110V 1A
  接 CDI 2P 右(黑紅) 激磁
  輸出約 AC 170V
  1KΩ 1KΩ
  10KΩ
  10KΩ
  NSR150 CDI
  4P 左上(綠) 接地
  4P 右下(黑黃) 點火線圈

custom parts:
  TM1637: A 4 7-seg display
  Mini-360 DC-DC Buck converter: Mini-360 DC-DC Buck converter. Tiny buck step down voltage converter, input voltage 4.75 to 23V output 1 to 17V adjustable. Available from ebay and the like.
  74LS04: Hex Inverter
  74LS04: Hex Inverter
  74LS04: Hex Inverter
  74LS04: Hex Inverter
  74LS04: Hex Inverter
  74LS04: Hex Inverter
  74LS04: Hex Inverter
  74LS04: Hex Inverter
