# Fritzing sketch NSR_CDI_TESTER電路圖V0.02 (saved by Fritzing 0.9.3b)
breadboards: 2

parts:
  U1 = attiny85 [package=dip]
  元件1 = TM1637
  R1 = Rotary Potentiometer (Large) [maximum_resistance=100kΩ package=THT]
  R2 = Resistor [tolerance=±5% resistance=100 package="0402 [SMD]"]
  LED1 = LED - 5mm [color="Red (633nm)" package="5 mm [THT]"]
  U2 = Sharp PC817 [package=THT]
  R3 = Resistor [tolerance=±5% resistance=10k package=THT]
  R4 = Resistor [tolerance=±5% resistance=10k package=THT]
  U3 = Transformer [package=transformer]
  Q1 = TRANSISTOR_NPN [package=to-92]
  Q3 = TRANSISTOR_NPN [package=to-92]
  R11 = Resistor [tolerance=±5% resistance=1k package=THT]
  U5 = Transformer [package=transformer]
  IC1 = General purpose bipolar Timer [package=dil-08]
  R12 = Resistor [tolerance=±5% resistance=1k package=THT]
  R13 = Resistor [tolerance=±5% resistance=22k package=THT]
  C1 = Electrolytic Capacitor [capacitance=100nF voltage=35V package="100 mil [THT, electrolytic]"]
  R14 = Resistor [tolerance=±5% resistance=4.7k package=THT]
  R15 = Resistor [tolerance=±5% resistance=10k package=THT]
  R16 = Resistor [tolerance=±5% resistance=220 package=THT]
  R17 = Resistor [tolerance=±5% resistance=10k package=THT]
  C2 = Ceramic Capacitor [capacitance=100nF package="100 mil [THT, multilayer]"]
  D1 = Rectifier Diode [part_number=1N4001 package="300 mil [THT]"]
  D2 = Rectifier Diode [part_number=1N4001 package="300 mil [THT]"]
  D3 = Rectifier Diode [part_number=1N4001 package="300 mil [THT]"]

nets:
  N1: U1.Pin_2, R1.wiper
  N2: U1.Pin_3, R2.Pin_0
  N3: U1.Pin_4, 元件1.VCC, R1.leg2, U2.Pin_2, R3.Pin_0, D2.anode
  N4: U1.Pin_5, 元件1.CLK
  N5: U1.Pin_6, 元件1.DIO
  N6: U1.Pin_8, 元件1.GND, R1.leg1, D2.cathode
  N7: R2.Pin_1, LED1.anode
  N8: LED1.cathode, U2.Pin_1, R3.Pin_1
  N9: U2.Pin_4, D3.cathode
  N10: U2.Pin_3, R4.Pin_0
  N11: R4.Pin_1, U3.3, U5.4, D3.anode
  N12: Q1.E, Q3.C, IC1.GND, C1.-, R15.Pin_1, R17.Pin_1, C2.1, D1.anode
  N13: Q1.B, R11.Pin_1, R16.Pin_0
  N14: Q1.C, R14.Pin_1, R15.Pin_0
  N15: Q3.E, R16.Pin_1, R17.Pin_0
  N16: R11.Pin_0, IC1._RES, IC1.VCC+, R12.Pin_0, D1.cathode
  N17: IC1.TRI, IC1.TRE, R13.Pin_1, C1.+
  N18: IC1.OUT, R14.Pin_0
  N19: IC1.CON, C2.0
  N20: IC1.DIS, R12.Pin_1, R13.Pin_0

notes:
  接 CDI 4P 右上(青黃) 脈衝
  NSR-150
  CDI 點火測試機
  V0.02
  By 羽山 https://3wa.tw
  LED
  10KΩ
  PC817
  TM1637
  ATTiny 85
  VR 10KΩ
  100Ω
  小型變壓器
  ST-20 (600:1K)
  第三組獨立電源
  VCC 5V
  GND
  可用 USB 豆腐頭
  第一組獨立電源
  VCC 12V
  GND
  555
  第二組獨立電源
  VCC 5V
  GND
  可用 USB 豆腐頭
  1KΩ
  22KΩ
  4.7KΩ
  10KΩ
  C945
  腳BCE
  IRLZ48N
  腳GDS
  變壓器
  12-0
  110V 1A
  接 CDI 2P 右(黑紅) 激磁
  輸出約 AC 170V 320HZ
  1KΩ
  220Ω
  10KΩ
  NSR150 CDI
  4P 左上(綠) 接地
  4P 右下(黑黃) 點火線圈
  0.01㎌ (103)
  0.1㎌ / 35V
  TVS P6KE18A
  VCC 12V
  GND
  TVS P6KE6.8A

custom parts:
  TM1637: A 4 7-seg display
